# Fritzing sketch arduino-js-led (saved by Fritzing 0.9.3b)
breadboards: 1

parts:
  Part1 = Arduino Uno (Rev3) - ICSP
  LED1 = LED - 3mm [color="Red (633nm)" package="3 mm [THT]"]
  R1 = Resistor [tolerance=±5% resistance=220 package="2010 [SMD]"]

nets:
  N1: Part1.D8, R1.Pin_0
  N2: Part1.GND, LED1.cathode
  N3: LED1.anode, R1.Pin_1
