# Fritzing sketch arduino-photoresistor (saved by Fritzing 0.9.3b)
breadboards: 1

parts:
  Part1 = Arduino Uno (Rev3) - ICSP
  R2 = PHOTOCELL [package=photocell-kit]
  R1 = Resistor [tolerance=±5% resistance=220 package="2010 [SMD]"]

nets:
  N1: Part1.A0, R2.P$2, R1.Pin_1
  N2: Part1.5V, R2.P$1
  N3: Part1.GND, R1.Pin_0
